# Fritzing sketch gardmon (saved by Fritzing 0.9.3b)
breadboards: 1

parts:
  Part1 = Arduino Uno (Rev3)
  DHT1 = DHT22 Humidity and Temperature Sensor
  ZS-042_RTC1 = ZS-042 RTC Module
  R1 = Resistor [tolerance=±5% resistance=100k package=THT]
  U1 = mystery part, 16 pins [chip_label=DMD]

nets:
  N1: Part1.A4/SDA, ZS-042_RTC1.SDA
  N2: Part1.A5/SCL, ZS-042_RTC1.SCL
  N3: Part1.D8, U1.pin12
  N4: Part1.D9_PWM, U1.pin1
  N5: Part1.D11_PWM/MOSI, U1.pin11
  N6: Part1.D13/SCK, U1.pin13
  N7: Part1.D2, DHT1.DATA, R1.Pin_1
  N8: Part1.D6_PWM, U1.pin16
  N9: Part1.D7, U1.pin15
  5V: Part1.5V, DHT1.VDD, ZS-042_RTC1.VCC, R1.Pin_0
  GND: Part1.GND, DHT1.GND, ZS-042_RTC1.GND, U1.pin2, U1.pin3, U1.pin4, U1.pin5, U1.pin6, U1.pin7, U1.pin8
